# Fritzing sketch wiring (saved by Fritzing 0.9.4)
breadboards: 1

parts:
  Part1 = Arduino Uno (Rev3)
  HC-SR04_Sensor_1 = HC-SR04 Ultrasonic Distance Sensor
  U1 = 74HC595 [package="DIP16 [THT]"]
  LED1 = RGB LED (com. cathode, rbg) [package="5 mm [THT]"]
  LED2 = RGB LED (com. cathode, rbg) [package="5 mm [THT]"]
  R1 = Resistor [tolerance=±5% resistance=220 package="1206 [SMD]"]
  R2 = Resistor [tolerance=±5% resistance=220 package="1206 [SMD]"]
  R3 = Resistor [tolerance=±5% resistance=220 package="1206 [SMD]"]
  R4 = Resistor [tolerance=±5% resistance=220 package="1206 [SMD]"]
  R5 = Resistor [tolerance=±5% resistance=220 package="1206 [SMD]"]
  R6 = Resistor [tolerance=±5% resistance=220 package="1206 [SMD]"]

nets:
  VCC: Part1.5V, HC-SR04_Sensor_1.VCC, U1.MR, U1.VCC
  GND: Part1.GND, HC-SR04_Sensor_1.GND, U1.GND, LED1.common_cathode, LED2.common_cathode
  N1: U1.Q1, R1.Pin_0
  N2: U1.Q2, R2.Pin_0
  N3: U1.Q3, R3.Pin_0
  N4: U1.Q4, R4.Pin_0
  N5: U1.Q5, R5.Pin_0
  N6: U1.Q6, R6.Pin_0
  N7: LED1.red_anode, R1.Pin_1
  N8: LED1.blue_anode, R2.Pin_1
  N9: LED1.green_anode, R3.Pin_1
  N10: LED2.red_anode, R4.Pin_1
  N11: LED2.blue_anode, R5.Pin_1
  N12: LED2.green_anode, R6.Pin_1

notes:
  TODO: Display
